// Logisim project 12-bit RISC-V Processor-CS-Architecture.circ as structural Verilog
module BEQ_ic (
  input  [11:0] A,
  input  [11:0] B,
  output [11:0] res
);

  wire [11:0] adder_1_out;

  Adder #(.width(12)) adder_1 (.a(A), .b(B), .out(adder_1_out));  // open: cin, cout
  Subtractor #(.width(12)) subtractor_1 (.a(adder_1_out), .b(12'h1), .out(res));  // open: bin, bout
endmodule

module _12_bit_ALU (
  input  [11:0] B,
  input  [11:0] A,
  input  [1:0] ALU_OP,
  output Zero,
  output [11:0] Result,
  output [11:0] Cout
);

  wire adder_1_cout, subtractor_1_bout;
  wire [11:0] adder_1_out, bit_extender_1_out, bit_extender_2_out, divider_1_out, divider_1_rem,
       multiplier_1_cout, multiplier_1_out, subtractor_1_out;

  Adder #(.width(12)) adder_1 (.a(A), .b(B), .out(adder_1_out), .cout(adder_1_cout));  // open: cin
  Subtractor #(.width(12)) subtractor_1 (.a(A), .b(B), .out(subtractor_1_out), .bout(subtractor_1_bout));  // open: bin
  Multiplier #(.width(12)) multiplier_1 (.a(A), .b(B), .out(multiplier_1_out), .cout(multiplier_1_cout));  // open: cin
  Divider #(.width(12)) divider_1 (.a(A), .b(B), .out(divider_1_out), .rem(divider_1_rem));  // open: upper
  assign bit_extender_1_out = {{11{1'b0}}, adder_1_cout};  // Bit_Extender bit_extender_1
  assign bit_extender_2_out = {{11{1'b0}}, subtractor_1_bout};  // Bit_Extender bit_extender_2
  Multiplexer #(.select(2), .width(12), .enable("false")) multiplexer_1 (
    .in0(adder_1_out), .in1(subtractor_1_out), .in2(multiplier_1_out), .in3(divider_1_out), .out(Result),
    .sel(ALU_OP));
  Multiplexer #(.select(2), .width(12), .enable("false")) multiplexer_2 (
    .in0(bit_extender_1_out), .in1(bit_extender_2_out), .in2(multiplier_1_cout), .in3(divider_1_rem),
    .out(Cout), .sel(ALU_OP));
  nor nor_1 (Zero, Result[0], Result[1], Result[2], Result[3], Result[4], Result[5], Result[6], Result[7], Result[8], Result[9], Result[10], Result[11]);
endmodule

module _12_bit_register (
  input  [11:0] Write_Data,
  input  Write_Enabler,
  input  [2:0] Data1_RS,
  input  [2:0] RD,
  input  Clock,
  input  Register_Clear,
  input  [2:0] RT,
  output [11:0] Data1_RS_0caae8b2,
  output [11:0] Data_2_RT
);

  wire and_1_out, and_2_out, and_3_out, and_4_out, and_5_out, and_6_out, and_7_out, and_8_out,
       decoder_1_out0, decoder_1_out1, decoder_1_out2, decoder_1_out3, decoder_1_out4, decoder_1_out5,
       decoder_1_out6, decoder_1_out7;
  wire [11:0] register_1_q, register_2_q, register_3_q, register_4_q, register_5_q, register_6_q,
       register_7_q, register_8_q;

  Decoder #(.select(3), .enable("false")) decoder_1 (
    .out0(decoder_1_out0), .out1(decoder_1_out1), .out2(decoder_1_out2), .out3(decoder_1_out3),
    .out4(decoder_1_out4), .out5(decoder_1_out5), .out6(decoder_1_out6), .out7(decoder_1_out7), .sel(RD));
  and and_1 (and_1_out, decoder_1_out0, Write_Enabler);
  and and_2 (and_2_out, decoder_1_out1, Write_Enabler);
  and and_3 (and_3_out, decoder_1_out2, Write_Enabler);
  and and_4 (and_4_out, decoder_1_out3, Write_Enabler);
  and and_5 (and_5_out, decoder_1_out4, Write_Enabler);
  and and_6 (and_6_out, decoder_1_out5, Write_Enabler);
  and and_7 (and_7_out, decoder_1_out6, Write_Enabler);
  and and_8 (and_8_out, decoder_1_out7, Write_Enabler);
  Register #(.width(12)) register_1 (
    .D(Write_Data), .en(and_1_out), .Q(register_1_q), .clk(Clock), .clr(Register_Clear));
  Register #(.width(12)) register_2 (
    .D(Write_Data), .en(and_2_out), .Q(register_2_q), .clk(Clock), .clr(Register_Clear));
  Register #(.width(12)) register_3 (
    .D(Write_Data), .en(and_3_out), .Q(register_3_q), .clk(Clock), .clr(Register_Clear));
  Register #(.width(12)) register_4 (
    .D(Write_Data), .en(and_4_out), .Q(register_4_q), .clk(Clock), .clr(Register_Clear));
  Register #(.width(12)) register_5 (
    .D(Write_Data), .en(and_5_out), .Q(register_5_q), .clk(Clock), .clr(Register_Clear));
  Register #(.width(12)) register_6 (
    .D(Write_Data), .en(and_6_out), .Q(register_6_q), .clk(Clock), .clr(Register_Clear));
  Register #(.width(12)) register_7 (
    .D(Write_Data), .en(and_7_out), .Q(register_7_q), .clk(Clock), .clr(Register_Clear));
  Register #(.width(12)) register_8 (
    .D(Write_Data), .en(and_8_out), .Q(register_8_q), .clk(Clock), .clr(Register_Clear));
  Multiplexer #(.select(3), .width(12), .enable("false")) multiplexer_1 (
    .in0(register_1_q), .in1(register_2_q), .in2(register_3_q), .in3(register_4_q), .in4(register_5_q),
    .in5(register_6_q), .in6(register_7_q), .in7(register_8_q), .out(Data1_RS_0caae8b2), .sel(Data1_RS));
  Multiplexer #(.select(3), .width(12), .enable("false")) multiplexer_2 (
    .in0(register_1_q), .in1(register_2_q), .in2(register_3_q), .in3(register_4_q), .in4(register_5_q),
    .in5(register_6_q), .in6(register_7_q), .in7(register_8_q), .out(Data_2_RT), .sel(RT));
endmodule

module Control_unit (
  input  [2:0] Opcode,
  output Reg_Dst,
  output Write_Enb,
  output [1:0] ALU_op,
  output ALU_src,
  output Store_Enb,
  output Load_Enb,
  output RAM_to_Reg,
  output BEQ_control,
  output Jump
);

  wire and_1_out, and_2_out, and_3_out, and_5_out, and_6_out, and_7_out, and_8_out, not_1_out, not_2_out,
       not_3_out, not_4_out, not_5_out, not_6_out, not_7_out, not_8_out, not_9_out, not_10_out, not_11_out,
       not_12_out, not_13_out, not_14_out, not_15_out;

  not not_1 (not_1_out, Opcode[2]);
  not not_2 (not_2_out, Opcode[1]);
  not not_3 (not_3_out, Opcode[1]);
  not not_4 (not_4_out, Opcode[0]);
  not not_5 (not_5_out, Opcode[2]);
  not not_6 (not_6_out, Opcode[2]);
  not not_7 (not_7_out, Opcode[2]);
  not not_8 (not_8_out, Opcode[1]);
  not not_9 (not_9_out, Opcode[1]);
  not not_10 (not_10_out, Opcode[1]);
  not not_11 (not_11_out, Opcode[0]);
  not not_12 (not_12_out, Opcode[1]);
  not not_13 (not_13_out, Opcode[0]);
  not not_14 (not_14_out, Opcode[0]);
  and and_1 (and_1_out, not_1_out, Opcode[1]);
  and and_2 (and_2_out, Opcode[2], not_2_out);
  not not_15 (not_15_out, Opcode[2]);
  and and_3 (and_3_out, not_3_out, not_4_out);
  and and_4 (ALU_op[1], not_5_out, Opcode[1]);
  and and_5 (and_5_out, not_6_out, Opcode[0]);
  and and_6 (and_6_out, Opcode[1], Opcode[0]);
  and and_7 (and_7_out, not_7_out, Opcode[1]);
  and and_8 (and_8_out, Opcode[2], not_8_out);
  and and_9 (Store_Enb, Opcode[2], not_9_out, Opcode[0]);
  and and_10 (Load_Enb, Opcode[2], not_10_out, not_11_out);
  and and_11 (RAM_to_Reg, Opcode[2], not_12_out, not_13_out);
  and and_12 (BEQ_control, Opcode[2], Opcode[1], Opcode[0]);
  and and_13 (Jump, Opcode[2], Opcode[1], not_14_out);
  or or_1 (Reg_Dst, and_1_out, and_2_out);
  or or_2 (Write_Enb, not_15_out, and_3_out);
  or or_3 (ALU_op[0], and_5_out, and_6_out);
  or or_4 (ALU_src, and_7_out, and_8_out);
endmodule

module _12_bit_single_cycle_datapath (
  output [11:0] Jump_addr,
  output [11:0] Data_01,
  output [11:0] Data_02,
  output [11:0] Result,
  output [2:0] Opcode,
  output [2:0] Write_register,
  output [2:0] Rs,
  output [2:0] Rt,
  output [11:0] Next_inst,
  output [11:0] Cout___Rem
);

  wire and_1_out, button_1_out, button_2_out, clock_1_out, control_unit_1_alu_src,
       control_unit_1_beq_control, control_unit_1_jump, control_unit_1_load_enb, control_unit_1_ram_to_reg,
       control_unit_1_reg_dst, control_unit_1_store_enb, control_unit_1_write_enb, n12_bit_alu_1_zero,
       PC_clr_out;
  wire [1:0] control_unit_1_alu_op;
  wire [2:0] multiplexer_2_out;
  wire [11:0] beq_ic_1_res, bit_extender_1_out, multiplexer_1_out, multiplexer_3_out, n12_bit_alu_1_result,
       n12_bit_register_1_data_2_rt, PC_q, ram_1_data;

  Clock clock_1 (.out(clock_1_out));
  Control_unit control_unit_1 (
    .Opcode(Opcode), .Reg_Dst(control_unit_1_reg_dst), .Write_Enb(control_unit_1_write_enb),
    .ALU_op(control_unit_1_alu_op), .ALU_src(control_unit_1_alu_src), .Store_Enb(control_unit_1_store_enb),
    .Load_Enb(control_unit_1_load_enb), .RAM_to_Reg(control_unit_1_ram_to_reg),
    .BEQ_control(control_unit_1_beq_control), .Jump(control_unit_1_jump));
  Multiplexer #(.width(12), .enable("false")) multiplexer_1 (
    .in0(multiplexer_3_out), .in1(Jump_addr), .out(multiplexer_1_out), .sel(control_unit_1_jump));
  Register #(.width(12)) PC (.D(multiplexer_1_out), .Q(PC_q), .clk(clock_1_out), .clr(PC_clr_out));  // open: en
  Button PC_clr (.out(PC_clr_out));
  Adder #(.width(12)) adder_1 (.a(PC_q), .b(12'h1), .out({Jump_addr[11:9], Next_inst[8:0]}));  // open: cin, cout
  ROM #(.addrWidth(12), .dataWidth(12)) rom_1 (.addr(PC_q), .data({Opcode, Jump_addr[8:0]}));  // open: sel
  BEQ_ic beq_ic_1 (.A({Jump_addr[11:9], Next_inst[8:0]}), .B(bit_extender_1_out), .res(beq_ic_1_res));
  Multiplexer #(.width(3), .enable("false")) multiplexer_2 (
    .in0(Jump_addr[2:0]), .in1(Jump_addr[5:3]), .out(multiplexer_2_out), .sel(control_unit_1_reg_dst));
  assign bit_extender_1_out = {{9{1'b0}}, Jump_addr[2:0]};  // Bit_Extender bit_extender_1
  Multiplexer #(.width(12), .enable("false")) multiplexer_3 (
    .in0({Jump_addr[11:9], Next_inst[8:0]}), .in1(beq_ic_1_res), .out(multiplexer_3_out), .sel(and_1_out));
  and and_1 (and_1_out, n12_bit_alu_1_zero, control_unit_1_beq_control);
  _12_bit_register u_12_bit_register_1 (
    .Write_Data(Result), .Write_Enabler(control_unit_1_write_enb), .RD(multiplexer_2_out),
    .Clock(clock_1_out), .Data1_RS_0caae8b2(Data_01), .Data1_RS(Jump_addr[8:6]),
    .Data_2_RT(n12_bit_register_1_data_2_rt), .RT(Jump_addr[5:3]), .Register_Clear(button_1_out));
  Button button_1 (.out(button_1_out));
  Multiplexer #(.width(12), .enable("false")) multiplexer_4 (
    .in0(n12_bit_register_1_data_2_rt), .in1(bit_extender_1_out), .out(Data_02), .sel(control_unit_1_alu_src));
  _12_bit_ALU u_12_bit_alu_1 (
    .Zero(n12_bit_alu_1_zero), .Result(n12_bit_alu_1_result), .Cout(Cout___Rem), .B(Data_02), .A(Data_01),
    .ALU_OP(control_unit_1_alu_op));
  RAM #(.addrWidth(12), .dataWidth(12), .bus("separate")) ram_1 (
    .addr(n12_bit_alu_1_result), .din(n12_bit_register_1_data_2_rt), .data(ram_1_data),
    .str(control_unit_1_store_enb), .clk(clock_1_out), .ld(control_unit_1_load_enb), .clr(button_2_out));  // open: sel
  Button button_2 (.out(button_2_out));
  LED led_1 (.in(n12_bit_alu_1_zero));
  Multiplexer #(.width(12), .enable("false")) multiplexer_5 (
    .in0(n12_bit_alu_1_result), .in1(ram_1_data), .out(Result), .sel(control_unit_1_ram_to_reg));

  assign Next_inst[11:9] = Jump_addr[11:9];
  assign Rs = Jump_addr[8:6];
  assign Rt = Jump_addr[5:3];
  assign Write_register = Jump_addr[2:0];

  // Notes on the sheet:
  //   contents of rom_1 (hex, n*v repeats v):
  //   a 2e5 1bb 32e 5bd 60d 89c b2c c05 fbd a 2e5 1bb 32e c45 fbd a 2e5 1bb 32e c45
endmodule
